// Logisim project сдвигатель.circ as structural Verilog
module EVM (
  input  [7:0] x,
  input  [3:0] e,
  output [7:0] y
);

  wire not_1_out, not_2_out, not_3_out, not_4_out, or_1_out, or_2_out, or_3_out, or_4_out, or_5_out,
       or_6_out, or_7_out, or_8_out, or_9_out, or_10_out, or_11_out, or_12_out, or_13_out, or_14_out,
       or_15_out, or_16_out, or_17_out, or_18_out, or_19_out, or_20_out, or_21_out, or_22_out, or_23_out,
       or_24_out, or_25_out, or_26_out, or_27_out, or_28_out, or_29_out, or_30_out, or_31_out, or_32_out,
       or_33_out, or_34_out, or_35_out, or_36_out, or_37_out, or_38_out, or_39_out, or_40_out, or_41_out,
       or_42_out, or_43_out, or_44_out, or_45_out, or_46_out, or_47_out;

  not not_1 (not_1_out, e[3]);
  not not_2 (not_2_out, e[2]);
  not not_3 (not_3_out, e[1]);
  not not_4 (not_4_out, e[0]);
  or or_1 (or_1_out, x[7], not_4_out);
  or or_2 (or_2_out, x[7], not_3_out);
  or or_3 (or_3_out, x[7], not_2_out);
  or or_4 (or_4_out, x[7], not_1_out);
  or or_5 (or_5_out, x[6], e[3], e[2], e[1], e[0]);
  or or_6 (or_6_out, x[7], not_3_out);
  or or_7 (or_7_out, x[7], not_2_out);
  or or_8 (or_8_out, x[7], not_1_out);
  or or_9 (or_9_out, x[6], e[3], e[2], e[1], not_4_out);
  or or_10 (or_10_out, x[5], e[3], e[2], e[1], e[0]);
  or or_11 (or_11_out, x[7], not_2_out);
  or or_12 (or_12_out, x[7], not_1_out);
  or or_13 (or_13_out, x[7], not_3_out, not_4_out);
  or or_14 (or_14_out, x[5], e[3], e[2], e[1], not_4_out);
  or or_15 (or_15_out, x[6], e[3], e[2], not_3_out, e[0]);
  or or_16 (or_16_out, x[4], e[3], e[2], e[1], e[0]);
  or or_17 (or_17_out, x[7], not_2_out);
  or or_18 (or_18_out, x[7], not_1_out);
  or or_19 (or_19_out, x[3], e[3], e[2], e[1], e[0]);
  or or_20 (or_20_out, x[6], e[3], e[2], not_3_out, not_4_out);
  or or_21 (or_21_out, x[4], e[3], e[2], e[1], not_4_out);
  or or_22 (or_22_out, x[5], e[3], e[2], not_3_out, e[0]);
  or or_23 (or_23_out, x[7], not_1_out);
  or or_24 (or_24_out, x[7], not_2_out, not_4_out);
  or or_25 (or_25_out, x[7], not_2_out, not_3_out);
  or or_26 (or_26_out, x[6], e[3], not_2_out, e[1], e[0]);
  or or_27 (or_27_out, x[5], e[3], e[2], not_3_out, not_4_out);
  or or_28 (or_28_out, x[3], e[3], e[2], e[1], not_4_out);
  or or_29 (or_29_out, x[4], e[3], e[2], not_3_out, e[0]);
  or or_30 (or_30_out, x[2], e[3], e[2], e[1], e[0]);
  or or_31 (or_31_out, x[7], not_1_out);
  or or_32 (or_32_out, x[7], not_2_out, not_3_out);
  or or_33 (or_33_out, x[4], e[3], e[2], not_3_out, not_4_out);
  or or_34 (or_34_out, x[3], e[3], e[2], not_3_out, e[0]);
  or or_35 (or_35_out, x[6], e[3], not_2_out, e[1], not_4_out);
  or or_36 (or_36_out, x[1], e[3], e[2], e[1], e[0]);
  or or_37 (or_37_out, x[5], e[3], not_2_out, e[1], e[0]);
  or or_38 (or_38_out, x[2], e[3], e[2], e[1], not_4_out);
  or or_39 (or_39_out, x[7], not_1_out);
  or or_40 (or_40_out, x[7], not_2_out, not_3_out, not_4_out);
  or or_41 (or_41_out, x[3], e[3], e[2], not_3_out, not_4_out);
  or or_42 (or_42_out, x[5], e[3], not_2_out, e[1], not_4_out);
  or or_43 (or_43_out, x[6], e[3], not_2_out, not_3_out, e[0]);
  or or_44 (or_44_out, x[0], e[3], e[2], e[1], e[0]);
  or or_45 (or_45_out, x[1], e[3], e[2], e[1], not_4_out);
  or or_46 (or_46_out, x[2], e[3], e[2], not_3_out, e[0]);
  or or_47 (or_47_out, x[4], e[3], not_2_out, e[1], e[0]);
  and and_1 (y[6], or_1_out, or_2_out, or_3_out, or_4_out, or_5_out);
  and and_2 (y[5], or_6_out, or_7_out, or_8_out, or_9_out, or_10_out);
  and and_3 (y[4], or_11_out, or_12_out, or_13_out, or_14_out, or_15_out, or_16_out);
  and and_4 (y[3], or_17_out, or_18_out, or_19_out, or_20_out, or_21_out, or_22_out);
  and and_5 (y[2], or_23_out, or_24_out, or_25_out, or_26_out, or_27_out, or_28_out, or_29_out, or_30_out);
  and and_6 (y[1], or_31_out, or_32_out, or_33_out, or_34_out, or_35_out, or_36_out, or_37_out, or_38_out);
  and and_7 (y[0], or_39_out, or_40_out, or_41_out, or_42_out, or_43_out, or_44_out, or_45_out, or_46_out, or_47_out);

  assign y[7] = x[7];
endmodule

module MOYA (
  input  [2:0] e,
  input  [7:0] x,
  output [7:0] y
);

  wire ne0, ne1, ne2, or_1_out, or_2_out, or_3_out, or_4_out, or_5_out, or_6_out, or_7_out, or_8_out,
       or_9_out, or_10_out, or_11_out, or_12_out, or_13_out, or_14_out, or_15_out, or_16_out, or_17_out,
       or_18_out, or_19_out, or_20_out, or_21_out, or_22_out, or_23_out, or_24_out, or_25_out, or_26_out,
       or_27_out, or_28_out, or_29_out, or_30_out, or_31_out, or_32_out, or_33_out, or_34_out, or_35_out,
       or_36_out, or_37_out, or_38_out, or_39_out, or_40_out;

  not not_1 (ne2, e[2]);
  not not_2 (ne1, e[1]);
  not not_3 (ne0, e[0]);
  or or_1 (or_1_out, x[7], ne0);
  or or_2 (or_2_out, x[7], ne1);
  or or_3 (or_3_out, x[7], ne2);
  or or_4 (or_4_out, x[6], e[2], e[1], e[0]);
  and and_1 (y[6], or_1_out, or_2_out, or_3_out, or_4_out);
  or or_5 (or_5_out, x[7], ne1);
  or or_6 (or_6_out, x[7], ne2);
  or or_7 (or_7_out, x[6], e[2], e[1], ne0);
  or or_8 (or_8_out, x[5], e[2], e[1], e[0]);
  or or_9 (or_9_out, x[7], ne2);
  or or_10 (or_10_out, x[7], ne1, ne0);
  or or_11 (or_11_out, x[5], e[2], e[1], ne0);
  or or_12 (or_12_out, x[6], e[2], ne1, e[0]);
  or or_13 (or_13_out, x[4], e[2], e[1], e[0]);
  or or_14 (or_14_out, x[7], ne2);
  or or_15 (or_15_out, x[3], e[2], e[1], e[0]);
  or or_16 (or_16_out, x[6], e[2], ne1, ne0);
  or or_17 (or_17_out, x[4], e[2], e[1], ne0);
  or or_18 (or_18_out, x[5], e[2], ne1, e[0]);
  or or_19 (or_19_out, x[0], e[2], e[1], e[0]);
  or or_20 (or_20_out, x[1], e[2], e[1], ne0);
  or or_21 (or_21_out, x[2], e[2], ne1, e[0]);
  or or_22 (or_22_out, x[4], ne2, e[1], e[0]);
  or or_23 (or_23_out, x[7], ne2, ne1, ne0);
  or or_24 (or_24_out, x[3], e[2], ne1, ne0);
  or or_25 (or_25_out, x[5], ne2, e[1], ne0);
  or or_26 (or_26_out, x[6], ne2, ne1, e[0]);
  and and_2 (y[5], or_5_out, or_6_out, or_7_out, or_8_out);
  and and_3 (y[4], or_9_out, or_10_out, or_11_out, or_12_out, or_13_out);
  and and_4 (y[3], or_14_out, or_15_out, or_16_out, or_17_out, or_18_out);
  or or_27 (or_27_out, x[7], ne2, ne0);
  or or_28 (or_28_out, x[7], ne2, ne1);
  or or_29 (or_29_out, x[2], e[2], e[1], e[0]);
  or or_30 (or_30_out, x[6], ne2, e[1], e[0]);
  or or_31 (or_31_out, x[5], e[2], ne1, ne0);
  or or_32 (or_32_out, x[3], e[2], e[1], ne0);
  or or_33 (or_33_out, x[4], e[2], ne1, e[0]);
  or or_34 (or_34_out, x[7], ne2, ne1);
  or or_35 (or_35_out, x[1], e[2], e[1], e[0]);
  or or_36 (or_36_out, x[2], e[2], e[1], ne0);
  or or_37 (or_37_out, x[4], e[2], ne1, ne0);
  or or_38 (or_38_out, x[3], e[2], ne1, e[0]);
  or or_39 (or_39_out, x[6], ne2, e[1], ne0);
  or or_40 (or_40_out, x[5], ne2, e[1], e[0]);
  and and_5 (y[0], or_19_out, or_20_out, or_21_out, or_22_out, or_23_out, or_24_out, or_25_out, or_26_out);
  and and_6 (y[2], or_27_out, or_28_out, or_29_out, or_30_out, or_31_out, or_32_out, or_33_out);
  and and_7 (y[1], or_34_out, or_35_out, or_36_out, or_37_out, or_38_out, or_39_out, or_40_out);

  assign y[7] = x[7];
endmodule
