// Logisim project 8razrSummatorDvuxChiselVdvoichCode.circ as structural Verilog
module POS (
  input  o,
  input  i1,
  input  i2,
  output o2,
  output o1
);

  wire and_1_out, and_2_out, xor_1_out;

  or or_1 (o2, and_2_out, and_1_out);
  and and_1 (and_1_out, o, xor_1_out);
  xor xor_1 (xor_1_out, i1, i2);
  and and_2 (and_2_out, i1, i2);
  xor xor_2 (o1, xor_1_out, o);
endmodule

module VRS (
  input  in_1,
  input  in_2,
  input  in_3,
  input  in_4,
  input  in_5,
  input  in_6,
  input  in_7,
  input  in_8,
  input  in_9,
  input  in_10,
  input  in_11,
  input  in_12,
  input  in_13,
  input  in_14,
  input  in_15,
  input  in_16,
  input  in_17,
  output out_18,
  output out_19,
  output out_20,
  output out_21,
  output out_22,
  output out_23,
  output out_24,
  output out_25,
  output out_26
);

  wire pos_1_o2, pos_2_o2, pos_3_o2, pos_4_o2, pos_5_o2, pos_6_o2, pos_7_o2, pos_8_o2;

  POS pos_1 (.o(pos_2_o2), .i1(in_1), .i2(in_9), .o2(pos_1_o2), .o1(out_19));
  POS pos_2 (.o(pos_3_o2), .i1(in_2), .i2(in_10), .o2(pos_2_o2), .o1(out_20));
  POS pos_3 (.o(pos_4_o2), .i1(in_3), .i2(in_11), .o2(pos_3_o2), .o1(out_21));
  POS pos_4 (.o(pos_5_o2), .i1(in_4), .i2(in_12), .o2(pos_4_o2), .o1(out_22));
  POS pos_5 (.o(pos_6_o2), .i1(in_5), .i2(in_13), .o2(pos_5_o2), .o1(out_23));
  POS pos_6 (.o(pos_7_o2), .i1(in_6), .i2(in_14), .o2(pos_6_o2), .o1(out_24));
  POS pos_7 (.o(pos_8_o2), .i1(in_7), .i2(in_15), .o2(pos_7_o2), .o1(out_25));
  POS pos_8 (.o(in_17), .i1(in_8), .i2(in_16), .o2(pos_8_o2), .o1(out_26));
  xor xor_1 (out_18, pos_2_o2, pos_1_o2);
endmodule

module VRS_ext (
  input  in_1,
  input  in_2,
  input  in_3,
  input  in_4,
  input  in_5,
  input  in_6,
  input  in_7,
  input  in_8,
  input  in_9,
  input  in_10,
  input  in_11,
  input  in_12,
  input  in_13,
  input  in_14,
  input  in_15,
  input  in_16,
  input  in_17,
  output out_18,
  output out_19,
  output out_20,
  output out_21,
  output out_22,
  output out_23,
  output out_24,
  output out_25,
  output out_26,
  output out_27
);

  wire and_1_out, and_2_out, and_3_out, and_4_out, and_5_out, and_6_out, and_7_out, and_8_out, and_9_out,
       and_10_out, and_11_out, and_12_out, and_13_out, and_14_out, and_15_out, and_16_out, or_1_out,
       or_2_out, or_3_out, or_4_out, or_5_out, or_6_out, or_7_out, or_8_out, xor_2_out, xor_5_out, xor_7_out,
       xor_9_out, xor_11_out, xor_13_out, xor_15_out, xor_16_out;

  or or_1 (or_1_out, and_2_out, and_1_out);
  and and_1 (and_1_out, or_2_out, xor_2_out);
  and and_2 (and_2_out, in_1, in_9);
  xor xor_1 (out_19, xor_2_out, or_2_out);
  xor xor_2 (xor_2_out, in_1, in_9);
  xor xor_3 (out_18, or_1_out, or_2_out);
  or or_2 (or_2_out, and_3_out, and_4_out);
  and and_3 (and_3_out, in_2, in_10);
  xor xor_4 (out_21, xor_5_out, or_3_out);
  and and_4 (and_4_out, or_3_out, xor_5_out);
  xor xor_5 (xor_5_out, in_2, in_10);
  or or_3 (or_3_out, and_6_out, and_5_out);
  and and_5 (and_5_out, or_4_out, xor_7_out);
  and and_6 (and_6_out, in_3, in_11);
  xor xor_6 (out_22, xor_7_out, or_4_out);
  xor xor_7 (xor_7_out, in_3, in_11);
  and and_7 (and_7_out, in_4, in_12);
  or or_4 (or_4_out, and_7_out, and_8_out);
  xor xor_8 (out_23, xor_9_out, or_5_out);
  and and_8 (and_8_out, or_5_out, xor_9_out);
  xor xor_9 (xor_9_out, in_4, in_12);
  or or_5 (or_5_out, and_10_out, and_9_out);
  and and_9 (and_9_out, or_6_out, xor_11_out);
  and and_10 (and_10_out, in_5, in_13);
  xor xor_10 (out_24, xor_11_out, or_6_out);
  xor xor_11 (xor_11_out, in_5, in_13);
  and and_11 (and_11_out, in_6, in_14);
  or or_6 (or_6_out, and_11_out, and_12_out);
  xor xor_12 (out_25, xor_13_out, or_7_out);
  and and_12 (and_12_out, or_7_out, xor_13_out);
  xor xor_13 (xor_13_out, in_6, in_14);
  or or_7 (or_7_out, and_14_out, and_13_out);
  and and_13 (and_13_out, or_8_out, xor_15_out);
  and and_14 (and_14_out, in_7, in_15);
  xor xor_14 (out_26, xor_15_out, or_8_out);
  xor xor_15 (xor_15_out, in_7, in_15);
  or or_8 (or_8_out, and_16_out, and_15_out);
  and and_15 (and_15_out, in_17, xor_16_out);
  xor xor_16 (xor_16_out, in_8, in_16);
  and and_16 (and_16_out, in_8, in_16);
  xor xor_17 (out_27, xor_16_out, in_17);

  assign out_20 = out_19;

  // Other names for the same wires on the sheet: perepoln = out_18; y0 = out_27; y1 = out_26; y2 = out_25;
  //   y3 = out_24; y4 = out_23; y5 = out_22; y6 = out_21; y7 = out_19; znak = out_19
endmodule
