// Logisim project sdvigatel.circ as structural Verilog
module sdvig (
  input  in_1,
  input  in_2,
  input  in_3,
  input  in_4,
  input  in_5,
  input  in_6,
  input  in_7,
  input  in_8,
  input  in_9,
  input  in_10,
  input  in_11,
  input  in_12,
  output out_13,
  output out_14,
  output out_15,
  output out_16,
  output out_17,
  output out_18,
  output out_19,
  output out_20,
  output out_21
);

  wire and_1_out, and_2_out, not_1_out;

  Multiplexer multiplexer_1 (.in0(in_5), .in1(in_6), .out(out_14), .sel(in_4));
  not not_1 (not_1_out, in_3);
  Multiplexer multiplexer_2 (.in0(in_6), .in1(in_7), .out(out_15), .sel(in_4));
  and and_1 (and_1_out, in_1, not_1_out);
  and and_2 (and_2_out, in_2, in_3);
  Multiplexer multiplexer_3 (.in0(in_7), .in1(in_8), .out(out_16), .sel(in_4));
  or or_1 (out_13, and_1_out, and_2_out);
  Multiplexer multiplexer_4 (.in0(in_8), .in1(in_9), .out(out_17), .sel(in_4));
  Multiplexer multiplexer_5 (.in0(in_9), .in1(in_10), .out(out_18), .sel(in_4));
  Multiplexer multiplexer_6 (.in0(in_10), .in1(in_11), .out(out_19), .sel(in_4));
  Multiplexer multiplexer_7 (.in0(in_11), .in1(in_12), .out(out_20), .sel(in_4));
  Multiplexer multiplexer_8 (.in0(in_12), .in1(in_4), .out(out_21), .sel(in_4));
endmodule
